// Logisim project 2sComplementer.circ as structural Verilog: 1 circuit, main circuit main
module main (
  input  A,
  input  in_2,
  input  in_3,
  input  in_4,
  input  B,
  input  in_6,
  input  in_7,
  input  in_8,
  output out_9,
  output out_10,
  output out_11,
  output out_12,
  output out_13,
  output out_14,
  output out_15,
  output out_16
);

  wire n74283_1_pin2, n74283_1_pin3, n74283_1_pin5, n74283_1_pin14, n74283_2_pin2, n74283_2_pin3,
       n74283_2_pin5, n74283_2_pin14, xor_1_out, xor_5_out;

  xor xor_1 (xor_1_out, A, A);
  _74283 u_74283_1 (
    .pin1(out_15), .pin2(n74283_1_pin2), .pin3(n74283_1_pin3), .pin4(out_16), .pin5(n74283_1_pin5),
    .pin6(n74283_1_pin2), .pin7(A), .pin15(n74283_1_pin2), .pin14(n74283_1_pin14), .pin13(out_14),
    .pin12(xor_1_out), .pin11(n74283_1_pin2), .pin10(out_13));  // open: pin9
  xor xor_2 (n74283_1_pin14, A, in_2);
  xor xor_3 (n74283_1_pin3, A, in_3);
  xor xor_4 (n74283_1_pin5, A, in_4);
  xor xor_5 (xor_5_out, B, B);
  _74283 u_74283_2 (
    .pin1(out_11), .pin2(n74283_2_pin2), .pin3(n74283_2_pin3), .pin4(out_12), .pin5(n74283_2_pin5),
    .pin6(n74283_2_pin2), .pin7(B), .pin15(n74283_2_pin2), .pin14(n74283_2_pin14), .pin13(out_10),
    .pin12(xor_5_out), .pin11(n74283_2_pin2), .pin10(out_9));  // open: pin9
  xor xor_6 (n74283_2_pin14, B, in_6);
  xor xor_7 (n74283_2_pin3, B, in_7);
  xor xor_8 (n74283_2_pin5, B, in_8);
  // also tied to GND on the sheet: {n74283_1_pin2, n74283_2_pin2}
endmodule
