// Logisim project ADDSUB.circ as structural Verilog: 1 circuit, main circuit main
module main (
  input  A,
  input  in_2,
  input  in_3,
  input  in_4,
  input  SUB,
  input  B,
  input  in_7,
  input  in_8,
  input  in_9,
  output out_10,
  output out_11,
  output out_12,
  output out_13,
  output out_14
);

  wire n74283_1_pin2, n74283_1_pin6, n74283_1_pin11, n74283_1_pin15, not_1_out, xor_1_out, xor_2_out;

  xor xor_1 (xor_1_out, A, SUB);
  xor xor_2 (xor_2_out, A, n74283_1_pin11);
  not not_1 (not_1_out, xor_2_out);
  and and_1 (out_10, xor_1_out, not_1_out);
  _74283 u_74283_1 (
    .pin1(out_13), .pin2(n74283_1_pin2), .pin3(in_3), .pin4(out_14), .pin5(in_4), .pin6(n74283_1_pin6),
    .pin7(SUB), .pin15(n74283_1_pin15), .pin14(in_2), .pin13(out_12), .pin12(A), .pin11(n74283_1_pin11),
    .pin10(out_11));  // open: pin9
  xor xor_3 (n74283_1_pin11, SUB, B);
  xor xor_4 (n74283_1_pin15, SUB, in_7);
  xor xor_5 (n74283_1_pin2, SUB, in_8);
  xor xor_6 (n74283_1_pin6, SUB, in_9);
endmodule
