// Logisim project ALU.circ as structural Verilog: 6 circuits, main circuit main
module main (
  input  in_1,
  input  A,
  input  in_3,
  input  in_4,
  input  in_5,
  input  in_6,
  input  in_7,
  input  in_8,
  input  B
);

  wire absvalue_1_out_9, absvalue_1_out_10, absvalue_1_out_11, absvalue_1_out_12, absvalue_1_out_13,
       absvalue_1_out_14, absvalue_1_out_15, absvalue_1_out_16, addsub_1_out_10, addsub_1_out_11,
       addsub_1_out_12, addsub_1_out_13, addsub_1_out_14, comp_1_out_9, comp_1_out_10, comp_1_out_11,
       mul_1_out_9, mul_1_out_10, mul_1_out_11, mul_1_out_12, mul_1_out_13, mul_1_out_14, mul_1_out_15,
       mul_1_out_16;

  LED led_1 (.in(comp_1_out_9));
  LED led_2 (.in(comp_1_out_10));
  LED led_3 (.in(comp_1_out_11));
  ADDSUB addsub_1 (
    .A(A), .in_2(in_3), .in_3(in_4), .in_4(in_5), .SUB(in_1), .B(in_6), .in_7(in_7), .in_8(in_8), .in_9(B),
    .out_10(addsub_1_out_10), .out_11(addsub_1_out_11), .out_12(addsub_1_out_12), .out_13(addsub_1_out_13),
    .out_14(addsub_1_out_14));
  COMP comp_1 (
    .A(A), .in_2(in_3), .in_3(in_4), .in_4(in_5), .B(in_6), .in_6(in_7), .in_7(in_8), .in_8(B),
    .out_9(comp_1_out_9), .out_10(comp_1_out_10), .out_11(comp_1_out_11));
  LED led_4 (.in(mul_1_out_9));
  LED led_5 (.in(mul_1_out_10));
  LED led_6 (.in(mul_1_out_11));
  LED led_7 (.in(mul_1_out_12));
  LED led_8 (.in(mul_1_out_15));
  LED led_9 (.in(mul_1_out_13));
  LED led_10 (.in(mul_1_out_14));
  absValue absvalue_1 (
    .A(A), .in_2(in_3), .in_3(in_4), .in_4(in_5), .B(in_6), .in_6(in_7), .in_7(in_8), .in_8(B),
    .out_9(absvalue_1_out_9), .out_10(absvalue_1_out_10), .out_11(absvalue_1_out_11),
    .out_12(absvalue_1_out_12), .out_13(absvalue_1_out_13), .out_14(absvalue_1_out_14),
    .out_15(absvalue_1_out_15), .out_16(absvalue_1_out_16));
  LED led_11 (.in(mul_1_out_16));
  LED led_12 (.in(addsub_1_out_10));
  LED led_13 (.in(addsub_1_out_11));
  LED led_14 (.in(addsub_1_out_12));
  LED led_15 (.in(addsub_1_out_13));
  LED led_16 (.in(addsub_1_out_14));
  MUL mul_1 (
    .B(absvalue_1_out_9), .in_2(absvalue_1_out_10), .in_3(absvalue_1_out_11), .in_4(absvalue_1_out_12),
    .A(absvalue_1_out_13), .in_6(absvalue_1_out_14), .in_7(absvalue_1_out_15), .in_8(absvalue_1_out_16),
    .out_9(mul_1_out_9), .out_10(mul_1_out_10), .out_11(mul_1_out_11), .out_12(mul_1_out_12),
    .out_13(mul_1_out_13), .out_14(mul_1_out_14), .out_15(mul_1_out_15), .out_16(mul_1_out_16));

  // Notes on the sheet:
  //   SUB
  //   A>B
  //   A=B
  //   A<B
  //   A*B
  //   overflow
  //   +-A+-B
endmodule

module absValue (
  input  A,
  input  in_2,
  input  in_3,
  input  in_4,
  input  B,
  input  in_6,
  input  in_7,
  input  in_8,
  output out_9,
  output out_10,
  output out_11,
  output out_12,
  output out_13,
  output out_14,
  output out_15,
  output out_16
);

  wire n74283_1_pin2, n74283_1_pin3, n74283_1_pin5, n74283_1_pin14, n74283_2_pin2, n74283_2_pin3,
       n74283_2_pin5, n74283_2_pin14, xor_1_out, xor_5_out;

  xor xor_1 (xor_1_out, A, A);
  _74283 u_74283_1 (
    .pin1(out_15), .pin2(n74283_1_pin2), .pin3(n74283_1_pin3), .pin4(out_16), .pin5(n74283_1_pin5),
    .pin6(n74283_1_pin2), .pin7(A), .pin15(n74283_1_pin2), .pin14(n74283_1_pin14), .pin13(out_14),
    .pin12(xor_1_out), .pin11(n74283_1_pin2), .pin10(out_13));  // open: pin9
  xor xor_2 (n74283_1_pin14, A, in_2);
  xor xor_3 (n74283_1_pin3, A, in_3);
  xor xor_4 (n74283_1_pin5, A, in_4);
  xor xor_5 (xor_5_out, B, B);
  _74283 u_74283_2 (
    .pin1(out_11), .pin2(n74283_2_pin2), .pin3(n74283_2_pin3), .pin4(out_12), .pin5(n74283_2_pin5),
    .pin6(n74283_2_pin2), .pin7(B), .pin15(n74283_2_pin2), .pin14(n74283_2_pin14), .pin13(out_10),
    .pin12(xor_5_out), .pin11(n74283_2_pin2), .pin10(out_9));  // open: pin9
  xor xor_6 (n74283_2_pin14, B, in_6);
  xor xor_7 (n74283_2_pin3, B, in_7);
  xor xor_8 (n74283_2_pin5, B, in_8);
  // also tied to GND on the sheet: {n74283_1_pin2, n74283_2_pin2}
endmodule

module ADDSUB (
  input  A,
  input  in_2,
  input  in_3,
  input  in_4,
  input  SUB,
  input  B,
  input  in_7,
  input  in_8,
  input  in_9,
  output out_10,
  output out_11,
  output out_12,
  output out_13,
  output out_14
);

  wire n74283_1_pin2, n74283_1_pin6, n74283_1_pin11, n74283_1_pin15, not_1_out, xor_1_out, xor_2_out;

  xor xor_1 (xor_1_out, A, SUB);
  xor xor_2 (xor_2_out, A, n74283_1_pin11);
  not not_1 (not_1_out, xor_2_out);
  and and_1 (out_10, xor_1_out, not_1_out);
  _74283 u_74283_1 (
    .pin1(out_13), .pin2(n74283_1_pin2), .pin3(in_3), .pin4(out_14), .pin5(in_4), .pin6(n74283_1_pin6),
    .pin7(SUB), .pin15(n74283_1_pin15), .pin14(in_2), .pin13(out_12), .pin12(A), .pin11(n74283_1_pin11),
    .pin10(out_11));  // open: pin9
  xor xor_3 (n74283_1_pin11, SUB, B);
  xor xor_4 (n74283_1_pin15, SUB, in_7);
  xor xor_5 (n74283_1_pin2, SUB, in_8);
  xor xor_6 (n74283_1_pin6, SUB, in_9);
endmodule

module MUL (
  input  B,
  input  in_2,
  input  in_3,
  input  in_4,
  input  A,
  input  in_6,
  input  in_7,
  input  in_8,
  output out_9,
  output out_10,
  output out_11,
  output out_12,
  output out_13,
  output out_14,
  output out_15,
  output out_16
);

  wire and_1_out, and_2_out, and_3_out, and_4_out, and_5_out, and_6_out, and_7_out, and_8_out, and_9_out,
       and_10_out, and_11_out, and_12_out, and_16_out, n74283_1_pin1, n74283_1_pin2, n74283_1_pin3,
       n74283_1_pin4, n74283_1_pin5, n74283_1_pin10, n74283_1_pin13, n74283_2_pin1, n74283_2_pin2,
       n74283_2_pin3, n74283_2_pin4, n74283_2_pin5, n74283_2_pin10, n74283_2_pin13, n74283_2_pin14,
       n74283_3_pin1, n74283_3_pin3, n74283_3_pin4, n74283_3_pin5, n74283_3_pin7, n74283_3_pin9,
       n74283_3_pin10, n74283_3_pin12, n74283_3_pin13, n74283_3_pin14, n74283_4_pin3, n74283_4_pin4,
       n74283_4_pin5, n74283_4_pin12, n74283_4_pin14, n74283_5_pin2, n74283_5_pin3, n74283_5_pin5,
       n74283_5_pin7, n74283_5_pin14, n74283_6_pin3, n74283_6_pin4, n74283_6_pin5, n74283_6_pin12,
       n74283_7_pin2, n74283_7_pin3, n74283_7_pin5, xor_1_out, xor_2_out, xor_5_out, xor_9_out, xor_10_out,
       xor_14_out, xor_15_out;

  xor xor_1 (xor_1_out, A, A);
  xor xor_2 (xor_2_out, A, in_6);
  _74283 u_74283_1 (
    .pin1(n74283_1_pin1), .pin2(n74283_1_pin2), .pin3(n74283_1_pin3), .pin4(n74283_1_pin4),
    .pin5(n74283_1_pin5), .pin6(n74283_1_pin2), .pin7(A), .pin15(n74283_1_pin2), .pin14(xor_2_out),
    .pin13(n74283_1_pin13), .pin12(xor_1_out), .pin11(n74283_1_pin2), .pin10(n74283_1_pin10));  // open: pin9
  xor xor_3 (n74283_1_pin3, A, in_7);
  xor xor_4 (n74283_1_pin5, A, in_8);
  and and_1 (and_1_out, n74283_1_pin10, n74283_2_pin10);
  and and_2 (and_2_out, n74283_1_pin10, n74283_2_pin13);
  xor xor_5 (xor_5_out, B, B);
  _74283 u_74283_2 (
    .pin1(n74283_2_pin1), .pin2(n74283_2_pin2), .pin3(n74283_2_pin3), .pin4(n74283_2_pin4),
    .pin5(n74283_2_pin5), .pin6(n74283_2_pin2), .pin7(B), .pin15(n74283_2_pin2), .pin14(n74283_2_pin14),
    .pin13(n74283_2_pin13), .pin12(xor_5_out), .pin11(n74283_2_pin2), .pin10(n74283_2_pin10));  // open: pin9
  and and_3 (and_3_out, n74283_1_pin10, n74283_2_pin1);
  xor xor_6 (n74283_2_pin14, B, in_2);
  and and_4 (and_4_out, n74283_1_pin13, n74283_2_pin10);
  and and_5 (and_5_out, n74283_1_pin10, n74283_2_pin4);
  _74283 u_74283_3 (
    .pin1(n74283_3_pin1), .pin2(and_3_out), .pin3(n74283_3_pin3), .pin4(n74283_3_pin4), .pin5(n74283_3_pin5),
    .pin6(and_5_out), .pin7(n74283_3_pin7), .pin15(and_2_out), .pin14(n74283_3_pin14),
    .pin13(n74283_3_pin13), .pin12(n74283_3_pin12), .pin11(and_1_out), .pin10(n74283_3_pin10),
    .pin9(n74283_3_pin9));
  LED led_1 (.in(n74283_3_pin9));
  LED led_2 (.in(n74283_3_pin10));
  xor xor_7 (n74283_2_pin3, B, in_3);
  xor xor_8 (n74283_2_pin5, B, in_4);
  and and_6 (and_6_out, n74283_1_pin13, n74283_2_pin13);
  LED led_3 (.in(n74283_3_pin13));
  LED led_4 (.in(n74283_3_pin1));
  and and_7 (and_7_out, n74283_1_pin13, n74283_2_pin1);
  and and_8 (and_8_out, n74283_1_pin13, n74283_2_pin4);
  LED led_5 (.in(n74283_3_pin4));
  LED led_6 (.in(n74283_4_pin4));
  LED led_7 (.in(n74283_6_pin4));
  and and_9 (and_9_out, n74283_1_pin1, n74283_2_pin10);
  and and_10 (and_10_out, n74283_1_pin1, n74283_2_pin13);
  _74283 u_74283_4 (
    .pin1(n74283_3_pin5), .pin2(and_7_out), .pin3(n74283_4_pin3), .pin4(n74283_4_pin4), .pin5(n74283_4_pin5),
    .pin6(and_8_out), .pin7(n74283_3_pin7), .pin15(and_6_out), .pin14(n74283_4_pin14), .pin13(n74283_3_pin3),
    .pin12(n74283_4_pin12), .pin11(and_4_out), .pin10(n74283_3_pin14), .pin9(n74283_3_pin12));
  LED led_8 (.in(and_16_out));
  and and_11 (and_11_out, n74283_1_pin1, n74283_2_pin1);
  xor xor_9 (xor_9_out, n74283_3_pin9, xor_10_out);
  _74283 u_74283_5 (
    .pin1(out_11), .pin2(n74283_5_pin2), .pin3(n74283_5_pin3), .pin4(out_12), .pin5(n74283_5_pin5),
    .pin6(n74283_5_pin2), .pin7(n74283_5_pin7), .pin15(n74283_5_pin2), .pin14(n74283_5_pin14),
    .pin13(out_10), .pin12(xor_9_out), .pin11(n74283_5_pin2), .pin10(out_9));  // open: pin9
  xor xor_10 (xor_10_out, B, A);
  and and_12 (and_12_out, n74283_1_pin1, n74283_2_pin4);
  _74283 u_74283_6 (
    .pin1(n74283_4_pin5), .pin2(and_11_out), .pin3(n74283_6_pin3), .pin4(n74283_6_pin4),
    .pin5(n74283_6_pin5), .pin6(and_12_out), .pin7(n74283_3_pin7), .pin15(and_10_out), .pin14(n74283_3_pin7),
    .pin13(n74283_4_pin3), .pin12(n74283_6_pin12), .pin11(and_9_out), .pin10(n74283_4_pin14),
    .pin9(n74283_4_pin12));
  xor xor_11 (n74283_5_pin14, xor_10_out, n74283_3_pin10);
  xor xor_12 (n74283_5_pin3, xor_10_out, n74283_3_pin13);
  xor xor_13 (n74283_5_pin5, xor_10_out, n74283_3_pin1);
  and and_13 (n74283_6_pin12, n74283_1_pin4, n74283_2_pin10);
  and and_14 (n74283_6_pin3, n74283_1_pin4, n74283_2_pin13);
  and and_15 (n74283_6_pin5, n74283_1_pin4, n74283_2_pin1);
  xor xor_14 (xor_14_out, n74283_3_pin4, xor_10_out);
  xor xor_15 (xor_15_out, xor_10_out, n74283_4_pin4);
  _74283 u_74283_7 (
    .pin1(out_15), .pin2(n74283_7_pin2), .pin3(n74283_7_pin3), .pin4(out_16), .pin5(n74283_7_pin5),
    .pin6(n74283_7_pin2), .pin7(xor_10_out), .pin15(n74283_7_pin2), .pin14(xor_15_out), .pin13(out_14),
    .pin12(xor_14_out), .pin11(n74283_7_pin2), .pin10(out_13), .pin9(n74283_5_pin7));
  and and_16 (and_16_out, n74283_1_pin4, n74283_2_pin4);
  xor xor_16 (n74283_7_pin3, xor_10_out, n74283_6_pin4);
  xor xor_17 (n74283_7_pin5, xor_10_out, and_16_out);
  // also tied to GND on the sheet: {n74283_1_pin2, n74283_2_pin2, n74283_5_pin2, n74283_3_pin7, n74283_7_pin2}
endmodule

module COMP (
  input  A,
  input  in_2,
  input  in_3,
  input  in_4,
  input  B,
  input  in_6,
  input  in_7,
  input  in_8,
  output out_9,
  output out_10,
  output out_11
);

  wire and_1_out, and_2_out, and_3_out, and_4_out, n7485_1_pin2, n7485_1_pin3, n7485_1_pin5, n7485_1_pin7,
       not_1_out, not_2_out, not_3_out, xor_1_out;

  xor xor_1 (xor_1_out, A, B);
  not not_1 (not_1_out, xor_1_out);
  and and_1 (and_1_out, not_1_out, n7485_1_pin5);
  or or_1 (out_9, and_1_out, and_2_out);
  not not_2 (not_2_out, A);
  and and_2 (and_2_out, not_2_out, B);
  _7485 u_7485_1 (
    .pin1(B), .pin2(n7485_1_pin2), .pin3(n7485_1_pin3), .pin4(n7485_1_pin2), .pin5(n7485_1_pin5),
    .pin6(out_10), .pin7(n7485_1_pin7), .pin15(A), .pin14(in_6), .pin13(in_2), .pin12(in_3), .pin11(in_7),
    .pin10(in_4), .pin9(in_8));
  not not_3 (not_3_out, B);
  and and_3 (and_3_out, not_3_out, A);
  and and_4 (and_4_out, not_1_out, n7485_1_pin7);
  or or_2 (out_11, and_4_out, and_3_out);
  // also tied to GND on the sheet: n7485_1_pin2
  // also tied to VCC on the sheet: n7485_1_pin3

  // Notes on the sheet:
  //   A>B
  //   A>B
  //   a>b
  //   a<b
  //   a<b
  //   A=B
  //   A<B
  //   A<B
endmodule

module ALU (
  input  A,
  input  in_2,
  input  in_3,
  input  in_4,
  input  in_5,
  input  B,
  input  in_7,
  input  in_8,
  input  in_9,
  output out_10,
  output out_11,
  output out_12,
  output out_13,
  output out_14,
  output out_15,
  output out_16,
  output out_17,
  output out_18,
  output out_19,
  output out_20,
  output out_21,
  output out_22,
  output out_23,
  output out_24,
  output out_25
);

  wire and_2_out, and_3_out, and_4_out, and_5_out, and_6_out, and_7_out, and_8_out, and_9_out, and_10_out,
       and_11_out, and_12_out, and_13_out, and_14_out, and_15_out, and_16_out, and_17_out, and_21_out,
       n7485_1_pin2, n7485_1_pin3, n7485_1_pin5, n7485_1_pin7, n74283_1_pin2, n74283_1_pin6, n74283_1_pin11,
       n74283_1_pin15, n74283_2_pin1, n74283_2_pin2, n74283_2_pin3, n74283_2_pin4, n74283_2_pin5,
       n74283_2_pin10, n74283_2_pin13, n74283_3_pin1, n74283_3_pin2, n74283_3_pin3, n74283_3_pin4,
       n74283_3_pin5, n74283_3_pin10, n74283_3_pin13, n74283_3_pin14, n74283_4_pin1, n74283_4_pin3,
       n74283_4_pin4, n74283_4_pin5, n74283_4_pin7, n74283_4_pin9, n74283_4_pin10, n74283_4_pin12,
       n74283_4_pin13, n74283_4_pin14, n74283_5_pin3, n74283_5_pin4, n74283_5_pin5, n74283_5_pin12,
       n74283_5_pin14, n74283_6_pin2, n74283_6_pin3, n74283_6_pin5, n74283_6_pin7, n74283_6_pin14,
       n74283_7_pin3, n74283_7_pin4, n74283_7_pin5, n74283_7_pin12, n74283_8_pin2, n74283_8_pin3,
       n74283_8_pin5, not_1_out, not_2_out, not_3_out, not_4_out, undriven, xor_1_out, xor_2_out, xor_7_out,
       xor_8_out, xor_9_out, xor_12_out, xor_16_out, xor_17_out, xor_21_out, xor_22_out;

  xor xor_1 (xor_1_out, A, in_5);
  xor xor_2 (xor_2_out, A, n74283_1_pin11);
  not not_1 (not_1_out, xor_2_out);
  and and_1 (out_13, xor_1_out, not_1_out);
  _74283 u_74283_1 (
    .pin1(out_16), .pin2(n74283_1_pin2), .pin3(in_3), .pin4(out_17), .pin5(in_4), .pin6(n74283_1_pin6),
    .pin7(in_5), .pin15(n74283_1_pin15), .pin14(in_2), .pin13(out_15), .pin12(A), .pin11(n74283_1_pin11),
    .pin10(out_14));  // open: pin9
  xor xor_3 (n74283_1_pin11, in_5, B);
  xor xor_4 (n74283_1_pin15, in_5, in_7);
  xor xor_5 (n74283_1_pin6, in_5, in_9);
  xor xor_6 (n74283_1_pin2, in_5, in_8);
  xor xor_7 (xor_7_out, A, B);
  not not_2 (not_2_out, xor_7_out);
  and and_2 (and_2_out, not_2_out, n7485_1_pin5);
  not not_3 (not_3_out, A);
  and and_3 (and_3_out, not_3_out, B);
  or or_1 (out_10, and_2_out, and_3_out);
  _7485 u_7485_1 (
    .pin1(B), .pin2(n7485_1_pin2), .pin3(n7485_1_pin3), .pin4(n7485_1_pin2), .pin5(n7485_1_pin5),
    .pin6(out_11), .pin7(n7485_1_pin7), .pin15(A), .pin14(in_7), .pin13(in_2), .pin12(in_3), .pin11(in_8),
    .pin10(in_4), .pin9(in_9));
  and and_4 (and_4_out, not_2_out, n7485_1_pin7);
  not not_4 (not_4_out, B);
  and and_5 (and_5_out, not_4_out, A);
  or or_2 (out_12, and_4_out, and_5_out);
  xor xor_8 (xor_8_out, A, A);
  xor xor_9 (xor_9_out, A, in_2);
  _74283 u_74283_2 (
    .pin1(n74283_2_pin1), .pin2(n74283_2_pin2), .pin3(n74283_2_pin3), .pin4(n74283_2_pin4),
    .pin5(n74283_2_pin5), .pin6(n74283_2_pin2), .pin7(A), .pin15(n74283_2_pin2), .pin14(xor_9_out),
    .pin13(n74283_2_pin13), .pin12(xor_8_out), .pin11(n74283_2_pin2), .pin10(n74283_2_pin10));  // open: pin9
  xor xor_10 (n74283_2_pin3, A, undriven);
  and and_6 (and_6_out, n74283_2_pin10, n74283_3_pin10);
  xor xor_11 (n74283_2_pin5, A, in_4);
  and and_7 (and_7_out, n74283_2_pin10, n74283_3_pin13);
  xor xor_12 (xor_12_out, B, B);
  _74283 u_74283_3 (
    .pin1(n74283_3_pin1), .pin2(n74283_3_pin2), .pin3(n74283_3_pin3), .pin4(n74283_3_pin4),
    .pin5(n74283_3_pin5), .pin6(n74283_3_pin2), .pin7(B), .pin15(n74283_3_pin2), .pin14(n74283_3_pin14),
    .pin13(n74283_3_pin13), .pin12(xor_12_out), .pin11(n74283_3_pin2), .pin10(n74283_3_pin10));  // open: pin9
  and and_8 (and_8_out, n74283_2_pin10, n74283_3_pin1);
  xor xor_13 (n74283_3_pin14, B, in_7);
  xor xor_14 (n74283_3_pin3, B, in_8);
  and and_9 (and_9_out, n74283_2_pin13, n74283_3_pin10);
  and and_10 (and_10_out, n74283_2_pin10, n74283_3_pin4);
  _74283 u_74283_4 (
    .pin1(n74283_4_pin1), .pin2(and_8_out), .pin3(n74283_4_pin3), .pin4(n74283_4_pin4), .pin5(n74283_4_pin5),
    .pin6(and_10_out), .pin7(n74283_4_pin7), .pin15(and_7_out), .pin14(n74283_4_pin14),
    .pin13(n74283_4_pin13), .pin12(n74283_4_pin12), .pin11(and_6_out), .pin10(n74283_4_pin10),
    .pin9(n74283_4_pin9));
  LED led_1 (.in(n74283_4_pin9));
  LED led_2 (.in(n74283_4_pin10));
  xor xor_15 (n74283_3_pin5, B, in_9);
  and and_11 (and_11_out, n74283_2_pin13, n74283_3_pin13);
  and and_12 (and_12_out, n74283_2_pin13, n74283_3_pin1);
  LED led_3 (.in(n74283_4_pin13));
  LED led_4 (.in(n74283_4_pin1));
  LED led_5 (.in(n74283_4_pin4));
  and and_13 (and_13_out, n74283_2_pin1, n74283_3_pin10);
  and and_14 (and_14_out, n74283_2_pin13, n74283_3_pin4);
  LED led_6 (.in(n74283_5_pin4));
  LED led_7 (.in(n74283_7_pin4));
  and and_15 (and_15_out, n74283_2_pin1, n74283_3_pin13);
  _74283 u_74283_5 (
    .pin1(n74283_4_pin5), .pin2(and_12_out), .pin3(n74283_5_pin3), .pin4(n74283_5_pin4),
    .pin5(n74283_5_pin5), .pin6(and_14_out), .pin7(n74283_4_pin7), .pin15(and_11_out),
    .pin14(n74283_5_pin14), .pin13(n74283_4_pin3), .pin12(n74283_5_pin12), .pin11(and_9_out),
    .pin10(n74283_4_pin14), .pin9(n74283_4_pin12));
  LED led_8 (.in(and_21_out));
  and and_16 (and_16_out, n74283_2_pin1, n74283_3_pin1);
  xor xor_16 (xor_16_out, n74283_4_pin9, xor_17_out);
  _74283 u_74283_6 (
    .pin1(out_20), .pin2(n74283_6_pin2), .pin3(n74283_6_pin3), .pin4(out_21), .pin5(n74283_6_pin5),
    .pin6(n74283_6_pin2), .pin7(n74283_6_pin7), .pin15(n74283_6_pin2), .pin14(n74283_6_pin14),
    .pin13(out_19), .pin12(xor_16_out), .pin11(n74283_6_pin2), .pin10(out_18));  // open: pin9
  xor xor_17 (xor_17_out, B, A);
  and and_17 (and_17_out, n74283_2_pin1, n74283_3_pin4);
  _74283 u_74283_7 (
    .pin1(n74283_5_pin5), .pin2(and_16_out), .pin3(n74283_7_pin3), .pin4(n74283_7_pin4),
    .pin5(n74283_7_pin5), .pin6(and_17_out), .pin7(n74283_4_pin7), .pin15(and_15_out), .pin14(n74283_4_pin7),
    .pin13(n74283_5_pin3), .pin12(n74283_7_pin12), .pin11(and_13_out), .pin10(n74283_5_pin14),
    .pin9(n74283_5_pin12));
  xor xor_18 (n74283_6_pin14, xor_17_out, n74283_4_pin10);
  xor xor_19 (n74283_6_pin3, xor_17_out, n74283_4_pin13);
  xor xor_20 (n74283_6_pin5, xor_17_out, n74283_4_pin1);
  and and_18 (n74283_7_pin12, n74283_2_pin4, n74283_3_pin10);
  and and_19 (n74283_7_pin3, n74283_2_pin4, n74283_3_pin13);
  and and_20 (n74283_7_pin5, n74283_2_pin4, n74283_3_pin1);
  xor xor_21 (xor_21_out, n74283_4_pin4, xor_17_out);
  xor xor_22 (xor_22_out, xor_17_out, n74283_5_pin4);
  _74283 u_74283_8 (
    .pin1(out_24), .pin2(n74283_8_pin2), .pin3(n74283_8_pin3), .pin4(out_25), .pin5(n74283_8_pin5),
    .pin6(n74283_8_pin2), .pin7(xor_17_out), .pin15(n74283_8_pin2), .pin14(xor_22_out), .pin13(out_23),
    .pin12(xor_21_out), .pin11(n74283_8_pin2), .pin10(out_22), .pin9(n74283_6_pin7));
  and and_21 (and_21_out, n74283_2_pin4, n74283_3_pin4);
  xor xor_23 (n74283_8_pin3, xor_17_out, n74283_7_pin4);
  xor xor_24 (n74283_8_pin5, xor_17_out, and_21_out);
  // also tied to GND on the sheet: {n7485_1_pin2, n74283_2_pin2, n74283_3_pin2, n74283_6_pin2, n74283_4_pin7, n74283_8_pin2}
  // also tied to VCC on the sheet: n7485_1_pin3

  // Notes on the sheet:
  //   B
  //   SUB
  //   A>B
  //   a>b
  //   A>B
  //   a<b
  //   a<b
  //   A<B
  //   A=B
  //   A<B
endmodule
