// Logisim project Comparator.circ as structural Verilog: 1 circuit, main circuit main
module main (
  input  A,
  input  in_2,
  input  in_3,
  input  in_4,
  input  B,
  input  in_6,
  input  in_7,
  input  in_8,
  output out_9,
  output out_10,
  output out_11
);

  wire and_1_out, and_2_out, and_3_out, and_4_out, n7485_1_pin2, n7485_1_pin3, n7485_1_pin5, n7485_1_pin7,
       not_1_out, not_2_out, not_3_out, xor_1_out;

  xor xor_1 (xor_1_out, A, B);
  not not_1 (not_1_out, xor_1_out);
  and and_1 (and_1_out, not_1_out, n7485_1_pin5);
  or or_1 (out_9, and_1_out, and_2_out);
  not not_2 (not_2_out, A);
  and and_2 (and_2_out, not_2_out, B);
  _7485 u_7485_1 (
    .pin1(B), .pin2(n7485_1_pin2), .pin3(n7485_1_pin3), .pin4(n7485_1_pin2), .pin5(n7485_1_pin5),
    .pin6(out_10), .pin7(n7485_1_pin7), .pin15(A), .pin14(in_6), .pin13(in_2), .pin12(in_3), .pin11(in_7),
    .pin10(in_4), .pin9(in_8));
  not not_3 (not_3_out, B);
  and and_3 (and_3_out, not_3_out, A);
  and and_4 (and_4_out, not_1_out, n7485_1_pin7);
  or or_2 (out_11, and_4_out, and_3_out);
  // also tied to GND on the sheet: n7485_1_pin2
  // also tied to VCC on the sheet: n7485_1_pin3

  // Notes on the sheet:
  //   A>B
  //   A>B
  //   a>b
  //   a<b
  //   a<b
  //   A=B
  //   A<B
  //   A<B
endmodule
