// Logisim project Multiplier.circ as structural Verilog: 1 circuit, main circuit main
module main (
  input  B,
  input  in_2,
  input  in_3,
  input  in_4,
  input  A,
  input  in_6,
  input  in_7,
  input  in_8,
  output out_9,
  output out_10,
  output out_11,
  output out_12,
  output out_13,
  output out_14,
  output out_15,
  output out_16
);

  wire and_1_out, and_2_out, and_3_out, and_4_out, and_5_out, and_6_out, and_7_out, and_8_out, and_9_out,
       and_10_out, and_11_out, and_12_out, and_16_out, n74283_1_pin1, n74283_1_pin2, n74283_1_pin3,
       n74283_1_pin4, n74283_1_pin5, n74283_1_pin10, n74283_1_pin13, n74283_2_pin1, n74283_2_pin2,
       n74283_2_pin3, n74283_2_pin4, n74283_2_pin5, n74283_2_pin10, n74283_2_pin13, n74283_2_pin14,
       n74283_3_pin1, n74283_3_pin3, n74283_3_pin4, n74283_3_pin5, n74283_3_pin7, n74283_3_pin9,
       n74283_3_pin10, n74283_3_pin12, n74283_3_pin13, n74283_3_pin14, n74283_4_pin3, n74283_4_pin4,
       n74283_4_pin5, n74283_4_pin12, n74283_4_pin14, n74283_5_pin2, n74283_5_pin3, n74283_5_pin5,
       n74283_5_pin7, n74283_5_pin14, n74283_6_pin3, n74283_6_pin4, n74283_6_pin5, n74283_6_pin12,
       n74283_7_pin2, n74283_7_pin3, n74283_7_pin5, xor_1_out, xor_2_out, xor_5_out, xor_9_out, xor_10_out,
       xor_14_out, xor_15_out;

  xor xor_1 (xor_1_out, A, A);
  xor xor_2 (xor_2_out, A, in_6);
  _74283 u_74283_1 (
    .pin1(n74283_1_pin1), .pin2(n74283_1_pin2), .pin3(n74283_1_pin3), .pin4(n74283_1_pin4),
    .pin5(n74283_1_pin5), .pin6(n74283_1_pin2), .pin7(A), .pin15(n74283_1_pin2), .pin14(xor_2_out),
    .pin13(n74283_1_pin13), .pin12(xor_1_out), .pin11(n74283_1_pin2), .pin10(n74283_1_pin10));  // open: pin9
  xor xor_3 (n74283_1_pin3, A, in_7);
  xor xor_4 (n74283_1_pin5, A, in_8);
  and and_1 (and_1_out, n74283_1_pin10, n74283_2_pin10);
  and and_2 (and_2_out, n74283_1_pin10, n74283_2_pin13);
  xor xor_5 (xor_5_out, B, B);
  _74283 u_74283_2 (
    .pin1(n74283_2_pin1), .pin2(n74283_2_pin2), .pin3(n74283_2_pin3), .pin4(n74283_2_pin4),
    .pin5(n74283_2_pin5), .pin6(n74283_2_pin2), .pin7(B), .pin15(n74283_2_pin2), .pin14(n74283_2_pin14),
    .pin13(n74283_2_pin13), .pin12(xor_5_out), .pin11(n74283_2_pin2), .pin10(n74283_2_pin10));  // open: pin9
  and and_3 (and_3_out, n74283_1_pin10, n74283_2_pin1);
  xor xor_6 (n74283_2_pin14, B, in_2);
  and and_4 (and_4_out, n74283_1_pin13, n74283_2_pin10);
  and and_5 (and_5_out, n74283_1_pin10, n74283_2_pin4);
  _74283 u_74283_3 (
    .pin1(n74283_3_pin1), .pin2(and_3_out), .pin3(n74283_3_pin3), .pin4(n74283_3_pin4), .pin5(n74283_3_pin5),
    .pin6(and_5_out), .pin7(n74283_3_pin7), .pin15(and_2_out), .pin14(n74283_3_pin14),
    .pin13(n74283_3_pin13), .pin12(n74283_3_pin12), .pin11(and_1_out), .pin10(n74283_3_pin10),
    .pin9(n74283_3_pin9));
  LED led_1 (.in(n74283_3_pin9));
  LED led_2 (.in(n74283_3_pin10));
  xor xor_7 (n74283_2_pin3, B, in_3);
  xor xor_8 (n74283_2_pin5, B, in_4);
  and and_6 (and_6_out, n74283_1_pin13, n74283_2_pin13);
  LED led_3 (.in(n74283_3_pin13));
  LED led_4 (.in(n74283_3_pin1));
  and and_7 (and_7_out, n74283_1_pin13, n74283_2_pin1);
  and and_8 (and_8_out, n74283_1_pin13, n74283_2_pin4);
  LED led_5 (.in(n74283_3_pin4));
  LED led_6 (.in(n74283_4_pin4));
  LED led_7 (.in(n74283_6_pin4));
  and and_9 (and_9_out, n74283_1_pin1, n74283_2_pin10);
  and and_10 (and_10_out, n74283_1_pin1, n74283_2_pin13);
  _74283 u_74283_4 (
    .pin1(n74283_3_pin5), .pin2(and_7_out), .pin3(n74283_4_pin3), .pin4(n74283_4_pin4), .pin5(n74283_4_pin5),
    .pin6(and_8_out), .pin7(n74283_3_pin7), .pin15(and_6_out), .pin14(n74283_4_pin14), .pin13(n74283_3_pin3),
    .pin12(n74283_4_pin12), .pin11(and_4_out), .pin10(n74283_3_pin14), .pin9(n74283_3_pin12));
  LED led_8 (.in(and_16_out));
  and and_11 (and_11_out, n74283_1_pin1, n74283_2_pin1);
  xor xor_9 (xor_9_out, n74283_3_pin9, xor_10_out);
  _74283 u_74283_5 (
    .pin1(out_11), .pin2(n74283_5_pin2), .pin3(n74283_5_pin3), .pin4(out_12), .pin5(n74283_5_pin5),
    .pin6(n74283_5_pin2), .pin7(n74283_5_pin7), .pin15(n74283_5_pin2), .pin14(n74283_5_pin14),
    .pin13(out_10), .pin12(xor_9_out), .pin11(n74283_5_pin2), .pin10(out_9));  // open: pin9
  xor xor_10 (xor_10_out, B, A);
  and and_12 (and_12_out, n74283_1_pin1, n74283_2_pin4);
  _74283 u_74283_6 (
    .pin1(n74283_4_pin5), .pin2(and_11_out), .pin3(n74283_6_pin3), .pin4(n74283_6_pin4),
    .pin5(n74283_6_pin5), .pin6(and_12_out), .pin7(n74283_3_pin7), .pin15(and_10_out), .pin14(n74283_3_pin7),
    .pin13(n74283_4_pin3), .pin12(n74283_6_pin12), .pin11(and_9_out), .pin10(n74283_4_pin14),
    .pin9(n74283_4_pin12));
  xor xor_11 (n74283_5_pin14, xor_10_out, n74283_3_pin10);
  xor xor_12 (n74283_5_pin3, xor_10_out, n74283_3_pin13);
  xor xor_13 (n74283_5_pin5, xor_10_out, n74283_3_pin1);
  and and_13 (n74283_6_pin12, n74283_1_pin4, n74283_2_pin10);
  and and_14 (n74283_6_pin3, n74283_1_pin4, n74283_2_pin13);
  and and_15 (n74283_6_pin5, n74283_1_pin4, n74283_2_pin1);
  xor xor_14 (xor_14_out, n74283_3_pin4, xor_10_out);
  xor xor_15 (xor_15_out, xor_10_out, n74283_4_pin4);
  _74283 u_74283_7 (
    .pin1(out_15), .pin2(n74283_7_pin2), .pin3(n74283_7_pin3), .pin4(out_16), .pin5(n74283_7_pin5),
    .pin6(n74283_7_pin2), .pin7(xor_10_out), .pin15(n74283_7_pin2), .pin14(xor_15_out), .pin13(out_14),
    .pin12(xor_14_out), .pin11(n74283_7_pin2), .pin10(out_13), .pin9(n74283_5_pin7));
  and and_16 (and_16_out, n74283_1_pin4, n74283_2_pin4);
  xor xor_16 (n74283_7_pin3, xor_10_out, n74283_6_pin4);
  xor xor_17 (n74283_7_pin5, xor_10_out, and_16_out);
  // also tied to GND on the sheet: {n74283_1_pin2, n74283_2_pin2, n74283_5_pin2, n74283_3_pin7, n74283_7_pin2}
endmodule
